// Logisim project floating-point-adder.circ as structural Verilog: 3 circuits, main circuit main
module main (
  input  [15:0] A,
  input  [15:0] B,
  output [11:0] out_3
);

  wire adder_1_cout;
  wire [3:0] exponentdiff_1_max_a_b, exponentdiff_2_abs_a_b, exponentdiff_3_abs_a_b;
  wire [10:0] shifter_1_out, shifter_2_out;
  wire [11:0] fraction_sign_set_1_f_prime, fraction_sign_set_2_f_prime;

  ExponentDiff exponentdiff_1 (.A(A[14:11]), .B(B[14:11]), .Max_A_B(exponentdiff_1_max_a_b));  // open: abs_A_B
  ExponentDiff exponentdiff_2 (
    .A(exponentdiff_1_max_a_b), .B(A[14:11]), .abs_A_B(exponentdiff_2_abs_a_b));  // open: Max_A_B
  Shifter #(.width(11), .shift("lr")) shifter_1 (.in(A[10:0]), .\dist (exponentdiff_2_abs_a_b), .out(shifter_1_out));
  ExponentDiff exponentdiff_3 (
    .A(exponentdiff_1_max_a_b), .B(B[14:11]), .abs_A_B(exponentdiff_3_abs_a_b));  // open: Max_A_B
  fraction_sign_set fraction_sign_set_1 (.F(shifter_1_out), .S(A[15]), .F_prime(fraction_sign_set_1_f_prime));
  Shifter #(.width(11), .shift("lr")) shifter_2 (.in(B[10:0]), .\dist (exponentdiff_3_abs_a_b), .out(shifter_2_out));
  fraction_sign_set fraction_sign_set_2 (.F(shifter_2_out), .S(B[15]), .F_prime(fraction_sign_set_2_f_prime));
  Adder #(.width(12)) adder_1 (
    .a(fraction_sign_set_2_f_prime), .b(fraction_sign_set_1_f_prime), .out(out_3), .cin(1'b0),
    .cout(adder_1_cout));
endmodule

module ExponentDiff (
  input  [3:0] A,
  input  [3:0] B,
  output [3:0] abs_A_B,
  output [3:0] Max_A_B
);

  wire subtractor_1_bout;
  wire [3:0] negator_1_out, subtractor_1_out;

  Subtractor #(.width(4)) subtractor_1 (.a(A), .b(B), .out(subtractor_1_out), .bout(subtractor_1_bout));  // open: bin
  Negator #(.width(4)) negator_1 (.in(subtractor_1_out), .out(negator_1_out));
  Multiplexer #(.width(4), .enable("false")) multiplexer_1 (
    .in0(subtractor_1_out), .in1(negator_1_out), .out(abs_A_B), .sel(subtractor_1_bout));
  Multiplexer #(.width(4), .enable("false")) multiplexer_2 (.in0(A), .in1(B), .out(Max_A_B), .sel(subtractor_1_bout));
endmodule

module fraction_sign_set (
  input  [10:0] F,
  input  S,
  output [11:0] F_prime
);

  wire [11:0] bit_extender_1_out, negator_1_out;

  assign bit_extender_1_out = {{1{1'b0}}, F};  // Bit_Extender bit_extender_1
  Negator #(.width(12)) negator_1 (.in(bit_extender_1_out), .out(negator_1_out));
  Multiplexer #(.width(12), .enable("false")) multiplexer_1 (
    .in0(bit_extender_1_out), .in1(negator_1_out), .out(F_prime), .sel(S));
endmodule
